// Logisim project ALU.circ as structural Verilog: 2 circuits, main circuit main
module main (
  input  in_1,
  input  [3:0] A,
  input  [3:0] B,
  output Zero,
  output [3:0] out_5,
  output Overflow
);

  wire fulladder_1_carryout, fulladder_2_carryout, fulladder_3_carryout, fulladder_4_carryout;

  FullAdder fulladder_1 (
    .CarryIn(fulladder_4_carryout), .in_2(A[3]), .in_3(B[3]), .Subtract(in_1), .out_5(out_5[3]),
    .CarryOut(fulladder_1_carryout));
  FullAdder fulladder_2 (
    .CarryIn(in_1), .in_2(A[0]), .in_3(B[0]), .Subtract(in_1), .out_5(out_5[0]),
    .CarryOut(fulladder_2_carryout));
  FullAdder fulladder_3 (
    .CarryIn(fulladder_2_carryout), .in_2(A[1]), .in_3(B[1]), .Subtract(in_1), .out_5(out_5[1]),
    .CarryOut(fulladder_3_carryout));
  FullAdder fulladder_4 (
    .CarryIn(fulladder_3_carryout), .in_2(A[2]), .in_3(B[2]), .Subtract(in_1), .out_5(out_5[2]),
    .CarryOut(fulladder_4_carryout));
  xor xor_1 (Overflow, fulladder_4_carryout, fulladder_1_carryout);
  nor nor_1 (Zero, out_5[0], out_5[1], out_5[2], out_5[3]);

  // Other names for the same wires on the sheet: O0 = out_5[0]; O1 = out_5[1]; O2 = out_5[2]; O3 = out_5[3];
  //   Sub = in_1

  // Notes on the sheet:
  //   Used for branching
endmodule

module FullAdder (
  input  CarryIn,
  input  in_2,
  input  in_3,
  input  Subtract,
  output out_5,
  output CarryOut
);

  wire and_1_out, and_2_out, and_3_out, B, not_1_out;

  not not_1 (not_1_out, in_3);
  Multiplexer #(.enable("false")) multiplexer_1 (.in0(in_3), .in1(not_1_out), .out(B), .sel(Subtract));
  and and_1 (and_1_out, CarryIn, in_2);
  and and_2 (and_2_out, CarryIn, B);
  and and_3 (and_3_out, in_2, B);
  xor odd_parity_1 (out_5, CarryIn, in_2, B);
  or or_1 (CarryOut, and_1_out, and_2_out, and_3_out);

  // Other names for the same wires on the sheet: A = in_2

  // Notes on the sheet:
  //   Takes two 1 bit inputs, subtract signal and carry-in, outputs 1 bit and carry out
endmodule
