// Logisim project RotR.circ as structural Verilog
module rotr (
  input  [15:0] in_1,
  input  [3:0] in_2,
  output [15:0] out_3
);

  wire [15:0] multiplexer_1_out, multiplexer_2_out, multiplexer_3_out, rot1_1_out_2, rot2_1_out_2,
       rot4_1_out_2, rot8_1_out_2;

  Multiplexer #(.width(16), .enable("false")) multiplexer_1 (
    .in0(in_1), .in1(rot1_1_out_2), .out(multiplexer_1_out), .sel(in_2[0]));
  rot1 rot1_1 (.in_1(in_1), .out_2(rot1_1_out_2));
  Multiplexer #(.width(16), .enable("false")) multiplexer_2 (
    .in0(multiplexer_1_out), .in1(rot2_1_out_2), .out(multiplexer_2_out), .sel(in_2[1]));
  rot2 rot2_1 (.in_1(multiplexer_1_out), .out_2(rot2_1_out_2));
  Multiplexer #(.width(16), .enable("false")) multiplexer_3 (
    .in0(multiplexer_2_out), .in1(rot4_1_out_2), .out(multiplexer_3_out), .sel(in_2[2]));
  rot4 rot4_1 (.in_1(multiplexer_2_out), .out_2(rot4_1_out_2));
  Multiplexer #(.width(16), .enable("false")) multiplexer_4 (
    .in0(multiplexer_3_out), .in1(rot8_1_out_2), .out(out_3), .sel(in_2[3]));
  rot8 rot8_1 (.in_1(multiplexer_3_out), .out_2(rot8_1_out_2));
endmodule

module rot1 (
  input  [15:0] in_1,
  output [15:0] out_2
);


  assign out_2 = {in_1[0], in_1[15:1]};

  // Other names for the same wires on the sheet: Rest[14:0] = in_1[15:1]
endmodule

module rot2 (
  input  [15:0] in_1,
  output [15:0] out_2
);

  wire [15:0] rot1_1_out_2;

  rot1 rot1_1 (.in_1(in_1), .out_2(rot1_1_out_2));
  rot1 rot1_2 (.in_1(rot1_1_out_2), .out_2(out_2));
endmodule

module rot4 (
  input  [15:0] in_1,
  output [15:0] out_2
);

  wire [15:0] rot2_1_out_2;

  rot2 rot2_1 (.in_1(in_1), .out_2(rot2_1_out_2));
  rot2 rot2_2 (.in_1(rot2_1_out_2), .out_2(out_2));
endmodule

module rot8 (
  input  [15:0] in_1,
  output [15:0] out_2
);

  wire [15:0] rot4_1_out_2;

  rot4 rot4_1 (.in_1(in_1), .out_2(rot4_1_out_2));
  rot4 rot4_2 (.in_1(rot4_1_out_2), .out_2(out_2));
endmodule
